// Logisim project adder4.circ as structural Verilog: 5 circuits, main circuit implementation
module implementation (
  input  [3:0] Ain,
  input  [3:0] Bin,
  input  Cinin,
  output [3:0] Sum_Out,
  output Carry_Out
);

  wire cout0, cout1, cout2, G0, G1, G2, P0, P1, P2;

  Ci3 ci3_1 (
    .A3(Ain[3]), .B3(Bin[3]), .cin3(cout2), .G0(G0), .P0(P0), .G1(G1), .P1(P1), .G2(G2), .P2(P2),
    .cout3(Carry_Out), .sum3(Sum_Out[3]));
  Ci2 ci2_1 (
    .A2(Ain[2]), .B2(Bin[2]), .cin2(cout1), .G0(G0), .P0(P0), .G1(G1), .P1(P1), .G2(G2), .cout2(cout2),
    .P2(P2), .sum2(Sum_Out[2]));
  Ci1 ci1_1 (
    .A1(Ain[1]), .B1(Bin[1]), .cin1(cout0), .G0(G0), .P0(P0), .G1(G1), .cout1(cout1), .P1(P1),
    .sum1(Sum_Out[1]));
  Ci0 ci0_1 (.A0(Ain[0]), .B0(Bin[0]), .cin0(Cinin), .G0(G0), .cout0(cout0), .P0(P0), .sum0(Sum_Out[0]));

  // Other names for the same wires on the sheet: A[3:0] = Ain; B[3:0] = Bin; Cin = Cinin; C3 = Carry_Out;
  //   cout3 = Carry_Out; Sum[3:0] = Sum_Out; sum0 = Sum_Out[0]; sum1 = Sum_Out[1]; sum2 = Sum_Out[2];
  //   sum3 = Sum_Out[3]
endmodule

module Ci0 (
  input  A0,
  input  B0,
  input  cin0,
  output G0,
  output cout0,
  output P0,
  output sum0
);

  wire and_2_out, xor_2_out;

  and and_1 (G0, A0, B0);
  xor xor_1 (P0, A0, B0);
  and and_2 (and_2_out, P0, cin0);
  xor xor_2 (xor_2_out, B0, A0);
  or or_1 (cout0, G0, and_2_out);
  xor xor_3 (sum0, xor_2_out, cin0);
endmodule

module Ci1 (
  input  A1,
  input  B1,
  input  cin1,
  input  G0,
  input  P0,
  output G1,
  output cout1,
  output P1,
  output sum1
);

  wire and_2_out, and_3_out, xor_2_out;

  xor xor_1 (P1, A1, B1);
  and and_1 (G1, A1, B1);
  and and_2 (and_2_out, P1, cin1, P0);
  xor xor_2 (xor_2_out, B1, A1);
  and and_3 (and_3_out, P1, G0);
  or or_1 (cout1, G1, and_3_out, and_2_out);
  xor xor_3 (sum1, xor_2_out, cin1);
endmodule

module Ci2 (
  input  A2,
  input  B2,
  input  cin2,
  input  G0,
  input  P0,
  input  G1,
  input  P1,
  output G2,
  output cout2,
  output P2,
  output sum2
);

  wire and_2_out, and_3_out, and_4_out, xor_2_out;

  xor xor_1 (P2, A2, B2);
  and and_1 (G2, A2, B2);
  and and_2 (and_2_out, P2, P0, P1, cin2);
  xor xor_2 (xor_2_out, B2, A2);
  and and_3 (and_3_out, G1, P2);
  and and_4 (and_4_out, G0, P1, P2);
  or or_1 (cout2, G2, and_3_out, and_4_out, and_2_out);
  xor xor_3 (sum2, xor_2_out, cin2);
endmodule

module Ci3 (
  input  A3,
  input  B3,
  input  cin3,
  input  G0,
  input  P0,
  input  G1,
  input  P1,
  input  G2,
  input  P2,
  output cout3,
  output sum3
);

  wire and_1_out, and_2_out, and_3_out, and_4_out, and_5_out, xor_1_out, xor_2_out;

  xor xor_1 (xor_1_out, A3, B3);
  and and_1 (and_1_out, A3, B3);
  xor xor_2 (xor_2_out, B3, A3);
  and and_2 (and_2_out, xor_1_out, G2);
  and and_3 (and_3_out, xor_1_out, P2, G1);
  and and_4 (and_4_out, xor_1_out, P2, P1, G0);
  and and_5 (and_5_out, xor_1_out, P2, P1, P0, cin3);
  xor xor_3 (sum3, xor_2_out, cin3);
  or or_1 (cout3, and_1_out, and_2_out, and_3_out, and_4_out, and_5_out);
endmodule
