// Logisim project bitcounter.circ as structural Verilog: 1 circuit, main circuit implementation
module implementation (
  input  [7:0] BitsIn,
  input  CountZerosIn,
  output [3:0] BitCountOut
);

  wire [3:0] bit_extender_1_out, bit_extender_2_out, subtractor_1_out, subtractor_2_out;

  Bit_Extender #(.out_width(4)) bit_extender_1 (.in(BitsIn), .out(bit_extender_1_out));
  Bit_Extender #(.out_width(4)) bit_extender_2 (.in(BitsIn), .out(bit_extender_2_out));
  Subtractor #(.width(4)) subtractor_1 (
    .a(bit_extender_1_out), .b(bit_extender_1_out), .out(subtractor_1_out));  // open: bin, bout
  Subtractor #(.width(4)) subtractor_2 (
    .a(bit_extender_2_out), .b(bit_extender_2_out), .out(subtractor_2_out));  // open: bin, bout
  Multiplexer #(.enable("false"), .width(4)) multiplexer_1 (
    .in0(subtractor_1_out), .in1(subtractor_2_out), .out(BitCountOut), .sel(CountZerosIn));

  // Other names for the same wires on the sheet: BitCount[3:0] = BitCountOut; Bits[7:0] = BitsIn;
  //   CountZeros = CountZerosIn
endmodule
