// Logisim project shifter.circ as structural Verilog: 5 circuits, main circuit implementation
module implementation (
  input  IsRightShiftIn,
  input  IsArithmeticIn,
  input  [1:0] ShiftAmountIn,
  input  [2:0] NumberIn,
  output [2:0] ShiftedNumberOut
);

  wire [2:0] shift0_1_out_2, shift1_1_out_4, shift2_1_out_4, shift3_1_out_4;

  shift0 shift0_1 (.num(NumberIn), .out_2(shift0_1_out_2));
  shift1 shift1_1 (.rshift(IsRightShiftIn), .num(NumberIn), .arith(IsArithmeticIn), .out_4(shift1_1_out_4));
  shift2 shift2_1 (.rshift(IsRightShiftIn), .num(NumberIn), .arith(IsArithmeticIn), .out_4(shift2_1_out_4));
  shift3 shift3_1 (.rshift(IsRightShiftIn), .num(NumberIn), .arith(IsArithmeticIn), .out_4(shift3_1_out_4));
  Multiplexer #(.enable("false"), .select(2), .width(3)) multiplexer_1 (
    .in0(shift0_1_out_2), .in1(shift1_1_out_4), .in2(shift2_1_out_4), .in3(shift3_1_out_4),
    .out(ShiftedNumberOut), .sel(ShiftAmountIn));

  // Other names for the same wires on the sheet: IsArithmetic = IsArithmeticIn; IsRightShift = IsRightShiftIn;
  //   Number[2:0] = NumberIn; ShiftAmount[1:0] = ShiftAmountIn; ShiftedNumber[2:0] = ShiftedNumberOut
endmodule

module shift0 (
  input  [2:0] num,
  output [2:0] out_2
);


  assign out_2 = num;
endmodule

module shift1 (
  input  rshift,
  input  [2:0] num,
  input  arith,
  output [2:0] out_4
);

  wire alwaysZero, and_1_out, and_2_out, multiplexer_1_out, multiplexer_4_out, not_1_out;

  not not_1 (not_1_out, rshift);
  and and_1 (and_1_out, rshift, num[2]);
  Multiplexer #(.enable("false")) multiplexer_1 (
    .in0(alwaysZero), .in1(and_1_out), .out(multiplexer_1_out), .sel(arith));
  and and_2 (and_2_out, rshift, num[0]);
  Multiplexer #(.enable("false")) multiplexer_2 (.in0(num[0]), .in1(num[2]), .out(out_4[1]), .sel(rshift));
  Multiplexer #(.enable("false")) multiplexer_3 (.in0(num[1]), .in1(multiplexer_1_out), .out(out_4[2]), .sel(rshift));
  and and_3 (alwaysZero, not_1_out, rshift);
  Multiplexer #(.enable("false")) multiplexer_4 (
    .in0(alwaysZero), .in1(and_2_out), .out(multiplexer_4_out), .sel(arith));
  Multiplexer #(.enable("false")) multiplexer_5 (.in0(multiplexer_4_out), .in1(num[1]), .out(out_4[0]), .sel(rshift));

  // Other names for the same wires on the sheet: arithm = arith; zero = num[0]; one = num[1]; two = num[2];
  //   R = rshift
endmodule

module shift2 (
  input  rshift,
  input  [2:0] num,
  input  arith,
  output [2:0] out_4
);

  wire alwaysZero, and_1_out, and_2_out, and_3_out, and_4_out, multiplexer_1_out, multiplexer_2_out,
       multiplexer_5_out, not_1_out;

  not not_1 (not_1_out, rshift);
  and and_1 (and_1_out, rshift, num[2]);
  and and_2 (and_2_out, rshift, num[2]);
  and and_3 (and_3_out, rshift, num[2]);
  Multiplexer #(.enable("false")) multiplexer_1 (
    .in0(and_3_out), .in1(and_2_out), .out(multiplexer_1_out), .sel(rshift));
  Multiplexer #(.enable("false")) multiplexer_2 (
    .in0(alwaysZero), .in1(and_1_out), .out(multiplexer_2_out), .sel(arith));
  and and_4 (and_4_out, rshift, num[0]);
  Multiplexer #(.enable("false")) multiplexer_3 (
    .in0(alwaysZero), .in1(multiplexer_1_out), .out(out_4[1]), .sel(arith));
  Multiplexer #(.enable("false")) multiplexer_4 (.in0(num[0]), .in1(multiplexer_2_out), .out(out_4[2]), .sel(rshift));
  and and_5 (alwaysZero, not_1_out, rshift);
  Multiplexer #(.enable("false")) multiplexer_5 (
    .in0(alwaysZero), .in1(and_4_out), .out(multiplexer_5_out), .sel(arith));
  Multiplexer #(.enable("false")) multiplexer_6 (.in0(multiplexer_5_out), .in1(num[2]), .out(out_4[0]), .sel(rshift));

  // Other names for the same wires on the sheet: arithm = arith; zero = num[0]; one = num[1]; two = num[2];
  //   R = rshift
endmodule

module shift3 (
  input  rshift,
  input  [2:0] num,
  input  arith,
  output [2:0] out_4
);

  wire alwaysZero, multiplexer_1_out, not_1_out;

  not not_1 (not_1_out, rshift);
  and and_1 (alwaysZero, not_1_out, rshift);
  Multiplexer #(.enable("false")) multiplexer_1 (.in0(alwaysZero), .in1(num[2]), .out(multiplexer_1_out), .sel(rshift));
  Multiplexer #(.enable("false")) multiplexer_2 (
    .in0(alwaysZero), .in1(multiplexer_1_out), .out(out_4[2]), .sel(arith));

  assign out_4[1:0] = {2{out_4[2]}};

  // Other names for the same wires on the sheet: zero = num[0]; one = num[1]; two = num[2]; R = rshift
endmodule
